// Logisim project hw4.circ as structural Verilog: 14 circuits, main circuit main
module main (
  input  reset
);

  wire ALUinB, and_1_out, Blt, bne, Clk, Dmre, Dmwe, Input, JAL, keyboard_1_avail, multiplexer_6_out,
       not_1_out, not_2_out, not_3_out, not_4_out, not_5_out, Output, Rdst, Rwd, Rwe, zerochecker_1_out_3;
  wire [1:0] JP;
  wire [2:0] ALUop, multiplexer_3_out, multiplexer_4_out, Rd, Rs, Rt, Shamt;
  wire [5:0] Immediate;
  wire [6:0] ascii_out_1_out_2, keyboard_1_data;
  wire [15:0] address, alu_1_output, bit_extender_1_out, buff1, Instruction, multiplexer_1_out,
       multiplexer_2_out, multiplexer_5_out, multiplexer_7_out, multiplexer_8_out, multiplexer_9_out,
       n16_bit_adder_1_output, n16_bit_adder_2_output, pc, ram_1_data, Read1_val, registerfile_1_readdata2;

  Clock clock_1 (.out(Clk));
  _16_bit_register u_16_bit_register_1 (.DATA_IN(multiplexer_9_out), .CLK(Clk), .WE(1'b1), .RS(reset), .DATA_SAVED(pc));
  _16_bit_Adder u_16_bit_adder_1 (.A(16'h1), .B(pc), .SUB(1'b0), .Output(n16_bit_adder_1_output));  // open: OVF
  Instruction_map instruction_map_1 (
    .Instruction(Instruction), .PC(pc), .SHAMT(Shamt), .RD(Rd), .RT(Rt), .RS(Rs), .Immediate(Immediate),
    .Address(address), .ALUop(ALUop), .Rwe(Rwe), .Rdst(Rdst), .ALUinB(ALUinB), .Rwd(Rwd), .Dmwe(Dmwe),
    .Dmre(Dmre), .bne(bne), .JP(JP), .Input(Input), .Output(Output), .blt(Blt), .jal(JAL));
  ROM #(.addrWidth(16), .dataWidth(16)) rom_1 (.addr(pc), .data(Instruction), .sel(1'b1));
  Multiplexer #(.width(16)) multiplexer_1 (
    .in0(multiplexer_2_out), .in1(buff1), .out(multiplexer_1_out), .sel(Input));  // open: en
  not not_1 (not_1_out, JAL);
  not not_2 (not_2_out, Clk);
  Multiplexer #(.width(16)) multiplexer_2 (
    .in0(n16_bit_adder_1_output), .in1(multiplexer_8_out), .out(multiplexer_2_out), .sel(not_1_out));  // open: en
  Keyboard keyboard_1 (.clk(Clk), .re(Input), .clr(reset), .avail(keyboard_1_avail), .data(keyboard_1_data));
  Multiplexer #(.width(3)) multiplexer_3 (.in0(Rd), .in1(Rt), .out(multiplexer_3_out), .sel(Rdst));  // open: en
  ASCII_inp ascii_inp_1 (.Data(keyboard_1_data), .Available(keyboard_1_avail), .OUTPUT(buff1));
  RegisterFile registerfile_1 (
    .DATA(multiplexer_1_out), .WE(Rwe), .RESET(reset), .R1(Rs), .R2(Rt), .WriteReg(multiplexer_4_out),
    .CLK(not_2_out), .ReadData1(Read1_val), .ReadData2(registerfile_1_readdata2));
  Multiplexer #(.width(3)) multiplexer_4 (
    .in0(multiplexer_3_out), .in1(3'b111), .out(multiplexer_4_out), .sel(JAL));  // open: en
  assign bit_extender_1_out = {{10{Immediate[5]}}, Immediate};  // Bit_Extender bit_extender_1
  Multiplexer #(.width(16)) multiplexer_5 (
    .in0(registerfile_1_readdata2), .in1(bit_extender_1_out), .out(multiplexer_5_out), .sel(ALUinB));  // open: en
  ASCII_out ascii_out_1 (.Data(Read1_val), .out_2(ascii_out_1_out_2));
  TTY #(.rows(13), .cols(80)) tty_1 (.data(ascii_out_1_out_2), .clk(not_3_out), .we(Output), .clr(reset));
  not not_3 (not_3_out, Clk);
  _16_bit_Adder u_16_bit_adder_2 (
    .A(n16_bit_adder_1_output), .B(bit_extender_1_out), .SUB(1'b0), .Output(n16_bit_adder_2_output));  // open: OVF
  ALU alu_1 (
    .OUTPUT(alu_1_output), .INPUT1(Read1_val), .INPUT2(multiplexer_5_out), .OPNUM(ALUop), .SHAMT(Shamt));  // open: OVF
  ZeroChecker zerochecker_1 (.Input(alu_1_output), .out_3(zerochecker_1_out_3), .CONTROL(Blt));
  not not_4 (not_4_out, zerochecker_1_out_3);
  Multiplexer multiplexer_6 (
    .in0(not_4_out), .in1(zerochecker_1_out_3), .out(multiplexer_6_out), .sel(Blt));  // open: en
  not not_5 (not_5_out, Clk);
  RAM #(.addrWidth(16), .dataWidth(16), .bus("separate")) ram_1 (
    .addr(alu_1_output), .din(registerfile_1_readdata2), .data(ram_1_data), .str(Dmwe), .clk(not_5_out),
    .ld(Dmre));  // open: sel, clr
  Multiplexer #(.width(16)) multiplexer_7 (
    .in0(n16_bit_adder_1_output), .in1(n16_bit_adder_2_output), .out(multiplexer_7_out), .sel(and_1_out));  // open: en
  and and_1 (and_1_out, bne, multiplexer_6_out);
  Multiplexer #(.width(16)) multiplexer_8 (
    .in0(alu_1_output), .in1(ram_1_data), .out(multiplexer_8_out), .sel(Rwd));  // open: en
  Multiplexer #(.select(2), .width(16)) multiplexer_9 (
    .in0(multiplexer_7_out), .in1(address), .in2(Read1_val), .in3(address), .out(multiplexer_9_out), .sel(JP));  // open: en

  // Notes on the sheet:
  //   Basic Control
  //   Instruction Translater
  //   Get the Instruction and store it in IM
  //   contents of rom_1 (hex, n*v repeats v):
  //   6083 60c4 6100 4825 6900 4825 6900 4821 6901 7940 7981 8880 88c1 6080 60c0 7880 78c1 91ff 6fc1 91ff
  //   Inputs
  //   convert input to 16-bit instruction
  //   Processing Unit
  //   Output Display
endmodule

module Instruction_map (
  input  [15:0] Instruction,
  input  [15:0] PC,
  output [2:0] SHAMT,
  output [2:0] RD,
  output [2:0] RT,
  output [2:0] RS,
  output [5:0] Immediate,
  output [15:0] Address,
  output [2:0] ALUop,
  output Rdst,
  output ALUinB,
  output Rwe,
  output jal,
  output Dmwe,
  output Rwd,
  output [1:0] JP,
  output bne,
  output Dmre,
  output Input,
  output Output,
  output blt
);

  wire add, addi, bne_t, I, J, j_t, jr, n0, n1, n2, n3, \not , or_3_out, or_8_out, or_13_out, R, sll, srl,
       sub, \xor ;

  not not_1 (n0, Instruction[15]);
  not not_2 (n2, Instruction[13]);
  not not_3 (n1, Instruction[14]);
  not not_4 (n3, Instruction[12]);
  and and_1 (add, n0, n1, n2, n3);
  and and_2 (addi, n0, Instruction[14], Instruction[13], n3);
  and and_3 (jr, Instruction[15], Instruction[14], n2, n3);
  assign SHAMT = R ? Instruction[2:0] : 3'bz;  // Controlled_Buffer controlled_buffer_1
  assign Immediate = I ? Instruction[5:0] : 6'bz;  // Controlled_Buffer controlled_buffer_2
  or or_1 (Rwe, jal, addi, \not , add, sub, \xor , srl, sll, Dmre, Input);
  or or_2 (R, add, sub, \not , \xor , sll, srl, jr);
  and and_4 (sub, n0, n1, n2, Instruction[12]);
  and and_5 (Dmre, n0, Instruction[14], Instruction[13], Instruction[12]);
  and and_6 (jal, Instruction[15], Instruction[14], n2, Instruction[12]);
  assign RD = R ? Instruction[5:3] : 3'bz;  // Controlled_Buffer controlled_buffer_3
  or or_3 (or_3_out, sub, bne_t, blt);
  or or_4 (ALUop[1], \xor , \not );
  or or_5 (ALUop[2], sll, srl);
  or or_6 (bne, bne_t, blt);
  or or_7 (ALUop[0], or_3_out, srl, \not );
  and and_7 (\not , n0, n1, Instruction[13], n3);
  and and_8 (Dmwe, Instruction[15], n1, n2, n3);
  and and_9 (Input, Instruction[15], Instruction[14], Instruction[13], n3);
  assign Address = J ? {PC[15:12], Instruction[11:0]} : 16'bz;  // Controlled_Buffer controlled_buffer_4
  assign RT = or_8_out ? Instruction[8:6] : 3'bz;  // Controlled_Buffer controlled_buffer_5
  or or_8 (or_8_out, R, I);
  or or_9 (JP[0], j_t, jal);
  or or_10 (JP[1], jr, jal);
  or or_11 (I, addi, Dmre, Dmwe, bne_t, blt, Input, Output);
  and and_10 (\xor , n0, n1, Instruction[13], Instruction[12]);
  and and_11 (bne_t, Instruction[15], n1, n2, Instruction[12]);
  and and_12 (Output, Instruction[15], Instruction[14], Instruction[13], Instruction[12]);
  or or_12 (Rdst, addi, Dmre, Dmwe, blt, Input, Output);
  and and_13 (sll, n0, Instruction[14], n2, n3);
  and and_14 (blt, Instruction[15], n1, Instruction[13], n3);
  assign RS = or_13_out ? Instruction[11:9] : 3'bz;  // Controlled_Buffer controlled_buffer_6
  or or_13 (or_13_out, R, I);
  or or_14 (ALUinB, Dmre, addi, Dmwe);
  and and_15 (srl, n0, Instruction[14], n2, Instruction[12]);
  and and_16 (j_t, Instruction[15], n1, Instruction[13], Instruction[12]);
  or or_15 (J, j_t, jal);

  assign Rwd = Dmre;

  // Other names for the same wires on the sheet: _0_2[2:0] = Instruction[2:0]; _3_5[2:0] = Instruction[5:3];
  //   _6_8[2:0] = Instruction[8:6]; _9_11[2:0] = Instruction[11:9]; _3 = Instruction[12]; _2 = Instruction[13];
  //   _1 = Instruction[14]; _0 = Instruction[15]; lw = Dmre; sw = Dmwe

  // Notes on the sheet:
  //   INSTRUCTION SET TYPES
  //   OPCODE => INSTRUCTION
  //   PROCESS THE INSTRUCTIONS
  //   CONTROL SIGNALS
  //   SHAMT is only for R-type instructions
  //   Divide rest of instruction for the ISA
  //   Immediate is only for I type
  //   Make the 4-bit opcode from the instruction
  //   Rd is only for R type instructions
  //   ALUop
  //   Write - Enable (Reg. File)
  //   -----------------------------------------------------------------------------------------------------------------------------------------------------------------------------------------------------------------------------------------------------------------------------------------------------------------------------------------------------------------------------------------------------
  //   -----------------------------------------------------------------------------------------------------------------------------------------------------------------------------------------------------------------------------------------------------------------------------------------------------------------------------------------------------------------------------------------------------
  //   -----------------------------------------------------------------------------------------------------------------------------------------------------------------------------------------------------------------------------------------------------------------------------------------------------------------------------------------------------------------------------------------------------
  //   00 - NO JUMP
  //   01 - J
  //   10 - JR
  //   11 - JAL
  //   RT is for both R & I instructions
  //   Collect all the R, I and J type instructions into R,I and J tunnels
  //   PC gives the opcode for the j-type instruction (only 4 bits)
  //   Get 11 bytes of jump-to from 0-11 bits of the instruction 
  //   Assign each instruction to its respective Opcode based on assignment document
  //   RS is for both R & I instructions
  //   Activate controls based on the instruction type
endmodule

// Register File
module RegisterFile (
  input  [15:0] DATA,
  input  WE,
  input  CLK,
  input  RESET,
  input  [2:0] R1,
  input  [2:0] R2,
  input  [2:0] WriteReg,
  output [15:0] ReadData1,
  output [15:0] ReadData2
);

  wire and_1_out, and_2_out, and_3_out, and_4_out, and_5_out, and_6_out, and_7_out, and_8_out,
       decoder_1_out0, decoder_1_out1, decoder_1_out2, decoder_1_out3, decoder_1_out4, decoder_1_out5,
       decoder_1_out6, decoder_1_out7, decoder_2_out0, decoder_2_out1, decoder_2_out2, decoder_2_out3,
       decoder_2_out4, decoder_2_out5, decoder_2_out6, decoder_2_out7, decoder_3_out0, decoder_3_out1,
       decoder_3_out2, decoder_3_out3, decoder_3_out4, decoder_3_out5, decoder_3_out6, decoder_3_out7;
  wire [15:0] n16_bit_register_1_data_saved, n16_bit_register_2_data_saved, n16_bit_register_3_data_saved,
       n16_bit_register_4_data_saved, n16_bit_register_5_data_saved, n16_bit_register_6_data_saved,
       n16_bit_register_7_data_saved, n16_bit_register_8_data_saved;

  Decoder #(.select(3)) decoder_1 (
    .out0(decoder_1_out0), .out1(decoder_1_out1), .out2(decoder_1_out2), .out3(decoder_1_out3),
    .out4(decoder_1_out4), .out5(decoder_1_out5), .out6(decoder_1_out6), .out7(decoder_1_out7), .sel(WriteReg));  // open: en
  and and_1 (and_1_out, decoder_1_out0, WE);
  and and_2 (and_2_out, decoder_1_out1, WE);
  and and_3 (and_3_out, decoder_1_out2, WE);
  and and_4 (and_4_out, decoder_1_out3, WE);
  and and_5 (and_5_out, decoder_1_out4, WE);
  and and_6 (and_6_out, decoder_1_out5, WE);
  and and_7 (and_7_out, decoder_1_out6, WE);
  and and_8 (and_8_out, decoder_1_out7, WE);
  // Probe on n16_bit_register_1_data_saved
  _16_bit_register u_16_bit_register_1 (
    .DATA_IN(DATA), .CLK(CLK), .WE(and_1_out), .RS(RESET), .DATA_SAVED(n16_bit_register_1_data_saved));
  _16_bit_register u_16_bit_register_2 (
    .DATA_IN(DATA), .CLK(CLK), .WE(and_2_out), .RS(RESET), .DATA_SAVED(n16_bit_register_2_data_saved));
  _16_bit_register u_16_bit_register_3 (
    .DATA_IN(DATA), .CLK(CLK), .WE(and_3_out), .RS(RESET), .DATA_SAVED(n16_bit_register_3_data_saved));
  _16_bit_register u_16_bit_register_4 (
    .DATA_IN(DATA), .CLK(CLK), .WE(and_4_out), .RS(RESET), .DATA_SAVED(n16_bit_register_4_data_saved));
  _16_bit_register u_16_bit_register_5 (
    .DATA_IN(DATA), .CLK(CLK), .WE(and_5_out), .RS(RESET), .DATA_SAVED(n16_bit_register_5_data_saved));
  _16_bit_register u_16_bit_register_6 (
    .DATA_IN(DATA), .CLK(CLK), .WE(and_6_out), .RS(RESET), .DATA_SAVED(n16_bit_register_6_data_saved));
  _16_bit_register u_16_bit_register_7 (
    .DATA_IN(DATA), .CLK(CLK), .WE(and_7_out), .RS(RESET), .DATA_SAVED(n16_bit_register_7_data_saved));
  _16_bit_register u_16_bit_register_8 (
    .DATA_IN(DATA), .CLK(CLK), .WE(and_8_out), .RS(RESET), .DATA_SAVED(n16_bit_register_8_data_saved));
  // Probe on n16_bit_register_2_data_saved
  // Probe on n16_bit_register_3_data_saved
  // Probe on n16_bit_register_4_data_saved
  // Probe on n16_bit_register_5_data_saved
  // Probe on n16_bit_register_6_data_saved
  // Probe on n16_bit_register_7_data_saved
  // Probe on n16_bit_register_8_data_saved
  assign ReadData1 = decoder_2_out0 ? n16_bit_register_1_data_saved : 16'bz;  // Controlled_Buffer controlled_buffer_1
  assign ReadData1 = decoder_2_out1 ? n16_bit_register_2_data_saved : 16'bz;  // Controlled_Buffer controlled_buffer_2
  Decoder #(.select(3)) decoder_2 (
    .out0(decoder_2_out0), .out1(decoder_2_out1), .out2(decoder_2_out2), .out3(decoder_2_out3),
    .out4(decoder_2_out4), .out5(decoder_2_out5), .out6(decoder_2_out6), .out7(decoder_2_out7), .sel(R1));  // open: en
  assign ReadData1 = decoder_2_out2 ? n16_bit_register_3_data_saved : 16'bz;  // Controlled_Buffer controlled_buffer_3
  assign ReadData1 = decoder_2_out3 ? n16_bit_register_4_data_saved : 16'bz;  // Controlled_Buffer controlled_buffer_4
  assign ReadData1 = decoder_2_out4 ? n16_bit_register_5_data_saved : 16'bz;  // Controlled_Buffer controlled_buffer_5
  assign ReadData1 = decoder_2_out5 ? n16_bit_register_6_data_saved : 16'bz;  // Controlled_Buffer controlled_buffer_6
  assign ReadData1 = decoder_2_out6 ? n16_bit_register_7_data_saved : 16'bz;  // Controlled_Buffer controlled_buffer_7
  assign ReadData1 = decoder_2_out7 ? n16_bit_register_8_data_saved : 16'bz;  // Controlled_Buffer controlled_buffer_8
  assign ReadData2 = decoder_3_out0 ? n16_bit_register_1_data_saved : 16'bz;  // Controlled_Buffer controlled_buffer_9
  Decoder #(.select(3)) decoder_3 (
    .out0(decoder_3_out0), .out1(decoder_3_out1), .out2(decoder_3_out2), .out3(decoder_3_out3),
    .out4(decoder_3_out4), .out5(decoder_3_out5), .out6(decoder_3_out6), .out7(decoder_3_out7), .sel(R2));  // open: en
  assign ReadData2 = decoder_3_out1 ? n16_bit_register_2_data_saved : 16'bz;  // Controlled_Buffer controlled_buffer_10
  assign ReadData2 = decoder_3_out2 ? n16_bit_register_3_data_saved : 16'bz;  // Controlled_Buffer controlled_buffer_11
  assign ReadData2 = decoder_3_out3 ? n16_bit_register_4_data_saved : 16'bz;  // Controlled_Buffer controlled_buffer_12
  assign ReadData2 = decoder_3_out4 ? n16_bit_register_5_data_saved : 16'bz;  // Controlled_Buffer controlled_buffer_13
  assign ReadData2 = decoder_3_out5 ? n16_bit_register_6_data_saved : 16'bz;  // Controlled_Buffer controlled_buffer_14
  assign ReadData2 = decoder_3_out6 ? n16_bit_register_7_data_saved : 16'bz;  // Controlled_Buffer controlled_buffer_15
  assign ReadData2 = decoder_3_out7 ? n16_bit_register_8_data_saved : 16'bz;  // Controlled_Buffer controlled_buffer_16

  // Notes on the sheet:
  //   $r0 is constant = 0, it cannot be changed ****
  //   $r6 is the stack pointer
  //   NOTES
  //   If Rd == Rs(R1) then data is written to readData1
  //   If Rd == Rt(R2) then data is written to readData2
  //   RS can be used to reset both the registers at same time
  //   $r7 is the link register for the jal instruction
endmodule

module _1_bit_Adder (
  input  A,
  input  B,
  input  C,
  output SUM,
  output CARRY
);

  wire AB_out, and_1_out, xor_1_out;

  xor xor_1 (xor_1_out, A, B);
  xor xor_2 (SUM, xor_1_out, C);
  and AB (AB_out, A, B);
  and and_1 (and_1_out, xor_1_out, C);
  or or_1 (CARRY, AB_out, and_1_out);

  // Notes on the sheet:
  //   A XOR B
  //   (A XOR B) XOR C
  //   (A XOR B).C
endmodule

module ALU (
  input  [15:0] INPUT1,
  input  [15:0] INPUT2,
  input  [2:0] OPNUM,
  input  [2:0] SHAMT,
  output [15:0] OUTPUT,
  output OVF
);

  wire n16_bit_adder_1_ovf, n16_bit_adder_2_ovf;
  wire [15:0] leftshift_1_output, n16_bit_adder_1_output, n16_bit_adder_2_output, not_1_out,
       rightshift_1_output, xor_1_out;

  _16_bit_Adder u_16_bit_adder_1 (
    .A(INPUT1), .B(INPUT2), .OVF(n16_bit_adder_1_ovf), .SUB(1'b0), .Output(n16_bit_adder_1_output));
  _16_bit_Adder u_16_bit_adder_2 (
    .A(INPUT1), .B(INPUT2), .OVF(n16_bit_adder_2_ovf), .SUB(1'b1), .Output(n16_bit_adder_2_output));
  assign xor_1_out = INPUT1 ^ INPUT2;  // XOR_Gate xor_1, 16 bits wide
  assign not_1_out = ~INPUT1;  // NOT_Gate not_1, 16 bits wide
  LeftShift leftshift_1 (.Input(INPUT1), .SHAMT(SHAMT), .Output(leftshift_1_output));
  RightShift rightshift_1 (.Input(INPUT1), .SHAMT(SHAMT), .Output(rightshift_1_output));
  Multiplexer #(.select(3), .width(16)) multiplexer_1 (
    .in0(n16_bit_adder_1_output), .in1(n16_bit_adder_2_output), .in2(xor_1_out), .in3(not_1_out),
    .in4(leftshift_1_output), .in5(rightshift_1_output), .in6({16{1'b0}}), .in7({16{1'b0}}), .out(OUTPUT),
    .sel(OPNUM));  // open: en
  Multiplexer #(.select(3)) multiplexer_2 (
    .in0(n16_bit_adder_1_ovf), .in1(n16_bit_adder_2_ovf), .in2(1'b0), .in3(1'b0), .in4(1'b0), .in5(1'b0),
    .in6(1'b0), .in7(1'b0), .out(OVF), .sel(OPNUM));  // open: en

  // Notes on the sheet:
  //   1. ADD - 000
  //   3. XOR - 010
  //   4. NOT A - 011
  //   TABLE OF INTRUCTIONS 
  //   2. SUBTRACT - 001
  //   5. LEFT SHIFT A - 100
  //   6. RIGHT SHIFT A - 101
endmodule

module LeftShift (
  input  [15:0] Input,
  input  [2:0] SHAMT,
  output [15:0] Output
);

  Multiplexer #(.select(3), .width(16)) multiplexer_1 (
    .in0(Input), .in1({Input[14:0], 1'b0}), .in2({Input[13:0], 2'b00}), .in3({Input[12:0], 3'b000}),
    .in4({Input[11:0], 4'b0000}), .in5({Input[10:0], {5{1'b0}}}), .in6({Input[9:0], {6{1'b0}}}),
    .in7({Input[8:0], {7{1'b0}}}), .out(Output), .sel(SHAMT));  // open: en

  // Other names for the same wires on the sheet: Left1[15:1] = Input[14:0]; Left2[15:2] = Input[13:0];
  //   Left3[15:3] = Input[12:0]; Left4[15:4] = Input[11:0]; Left5[15:5] = Input[10:0]; Left6[15:6] = Input[9:0];
  //   Left7[15:7] = Input[8:0]

  // Notes on the sheet:
  //   NOTES
  //   Shift the input to the left (multiply by 2^n)
endmodule

module RightShift (
  input  [15:0] Input,
  input  [2:0] SHAMT,
  output [15:0] Output
);

  Multiplexer #(.select(3), .width(16)) multiplexer_1 (
    .in0(Input), .in1({1'b0, Input[15:1]}), .in2({2'b00, Input[15:2]}), .in3({3'b000, Input[15:3]}),
    .in4({4'b0000, Input[15:4]}), .in5({{5{1'b0}}, Input[15:5]}), .in6({{6{1'b0}}, Input[15:6]}),
    .in7({{7{1'b0}}, Input[15:7]}), .out(Output), .sel(SHAMT));  // open: en

  // Other names for the same wires on the sheet: Left1[14:0] = Input[15:1]; Left2[13:0] = Input[15:2];
  //   Left3[12:0] = Input[15:3]; Left4[11:0] = Input[15:4]; Left5[10:0] = Input[15:5]; Left6[9:0] = Input[15:6];
  //   Left7[8:0] = Input[15:7]

  // Notes on the sheet:
  //   NOTES
  //   Shift the input to the right (divide by 2^n)
endmodule

module ZeroChecker (
  input  CONTROL,
  input  [15:0] Input,
  output out_3
);

  wire and_1_out, not_1_out, or_1_out;

  and and_1 (and_1_out, Input[15], 1'b1);
  or or_1 (or_1_out, Input[0], Input[1], Input[2], Input[3], Input[4], Input[5], Input[6], Input[7], Input[8], Input[9], Input[10], Input[11], Input[12], Input[13], Input[14], Input[15]);
  not not_1 (not_1_out, or_1_out);
  Multiplexer multiplexer_1 (.in0(not_1_out), .in1(and_1_out), .out(out_3), .sel(CONTROL));  // open: en

  // Notes on the sheet:
  //   NOTES
  //   If the MSB is 0, the number is positive
  //   If MSB is 1, the number is negative
  //   When CONTROL = 0, system checks for whether input is 0
  //   When control = 1, system checks if input is positive(0) or negative(1)
endmodule

module ASCII_inp (
  input  [6:0] Data,
  input  Available,
  output [15:0] OUTPUT
);

  Multiplexer #(.width(7)) multiplexer_1 (.in0({7{1'b0}}), .in1(Data), .out(OUTPUT[6:0]), .sel(Available));  // open: en
  not not_1 (OUTPUT[7], Available);

  assign OUTPUT[15:8] = {8{1'b0}};

  // Notes on the sheet:
  //   NOTES
  //   Read 6 bits of data if it is available
  //   7th bit is 1 only if data is available
  //   Last 8 should always be 0s
endmodule

module ASCII_out (
  input  [15:0] Data,
  output [6:0] out_2
);


  assign out_2 = Data[6:0];

  // Notes on the sheet:
  //   NOTES
  //   Read the first 6 bits of the data
endmodule

// PC
module _16_bit_register (
  input  [15:0] DATA_IN,
  input  CLK,
  input  WE,
  input  RS,
  output [15:0] DATA_SAVED
);

  D_Flip_Flop d_ff_1 (.clk(CLK), .D(DATA_IN[0]), .Q(DATA_SAVED[0]), .en(WE), .reset(RS));  // open: Qn, preset
  D_Flip_Flop d_ff_2 (.clk(CLK), .D(DATA_IN[1]), .Q(DATA_SAVED[1]), .en(WE), .reset(RS));  // open: Qn, preset
  D_Flip_Flop d_ff_3 (.clk(CLK), .D(DATA_IN[2]), .Q(DATA_SAVED[2]), .en(WE), .reset(RS));  // open: Qn, preset
  D_Flip_Flop d_ff_4 (.clk(CLK), .D(DATA_IN[3]), .Q(DATA_SAVED[3]), .en(WE), .reset(RS));  // open: Qn, preset
  D_Flip_Flop d_ff_5 (.clk(CLK), .D(DATA_IN[4]), .Q(DATA_SAVED[4]), .en(WE), .reset(RS));  // open: Qn, preset
  D_Flip_Flop d_ff_6 (.clk(CLK), .D(DATA_IN[5]), .Q(DATA_SAVED[5]), .en(WE), .reset(RS));  // open: Qn, preset
  D_Flip_Flop d_ff_7 (.clk(CLK), .D(DATA_IN[6]), .Q(DATA_SAVED[6]), .en(WE), .reset(RS));  // open: Qn, preset
  D_Flip_Flop d_ff_8 (.clk(CLK), .D(DATA_IN[7]), .Q(DATA_SAVED[7]), .en(WE), .reset(RS));  // open: Qn, preset
  D_Flip_Flop d_ff_9 (.clk(CLK), .D(DATA_IN[8]), .Q(DATA_SAVED[8]), .en(WE), .reset(RS));  // open: Qn, preset
  D_Flip_Flop d_ff_10 (.clk(CLK), .D(DATA_IN[9]), .Q(DATA_SAVED[9]), .en(WE), .reset(RS));  // open: Qn, preset
  D_Flip_Flop d_ff_11 (.clk(CLK), .D(DATA_IN[10]), .Q(DATA_SAVED[10]), .en(WE), .reset(RS));  // open: Qn, preset
  D_Flip_Flop d_ff_12 (.clk(CLK), .D(DATA_IN[11]), .Q(DATA_SAVED[11]), .en(WE), .reset(RS));  // open: Qn, preset
  D_Flip_Flop d_ff_13 (.clk(CLK), .D(DATA_IN[12]), .Q(DATA_SAVED[12]), .en(WE), .reset(RS));  // open: Qn, preset
  D_Flip_Flop d_ff_14 (.clk(CLK), .D(DATA_IN[13]), .Q(DATA_SAVED[13]), .en(WE), .reset(RS));  // open: Qn, preset
  D_Flip_Flop d_ff_15 (.clk(CLK), .D(DATA_IN[14]), .Q(DATA_SAVED[14]), .en(WE), .reset(RS));  // open: Qn, preset
  D_Flip_Flop d_ff_16 (.clk(CLK), .D(DATA_IN[15]), .Q(DATA_SAVED[15]), .en(WE), .reset(RS));  // open: Qn, preset

  // Other names for the same wires on the sheet: IN1 = DATA_IN[0]; IN2 = DATA_IN[1]; IN3 = DATA_IN[2];
  //   IN4 = DATA_IN[3]; IN5 = DATA_IN[4]; IN6 = DATA_IN[5]; IN7 = DATA_IN[6]; IN8 = DATA_IN[7]; IN9 = DATA_IN[8];
  //   IN10 = DATA_IN[9]; IN11 = DATA_IN[10]; IN12 = DATA_IN[11]; IN13 = DATA_IN[12]; IN14 = DATA_IN[13];
  //   IN15 = DATA_IN[14]; IN16 = DATA_IN[15]; OUT1 = DATA_SAVED[0]; OUT2 = DATA_SAVED[1]; OUT3 = DATA_SAVED[2];
  //   OUT4 = DATA_SAVED[3]; OUT5 = DATA_SAVED[4]; OUT6 = DATA_SAVED[5]; OUT7 = DATA_SAVED[6]; OUT8 = DATA_SAVED[7];
  //   OUT9 = DATA_SAVED[8]; OUT10 = DATA_SAVED[9]; OUT11 = DATA_SAVED[10]; OUT12 = DATA_SAVED[11];
  //   OUT13 = DATA_SAVED[12]; OUT14 = DATA_SAVED[13]; OUT15 = DATA_SAVED[14]; OUT16 = DATA_SAVED[15]

  // Notes on the sheet:
  //   RS resets 
  //   NOTES
  //   Writes data to the register on edge
  //   Clk  provides clock cycle edges
  //   WE tells when to write the data
endmodule

module _16_bit_Adder (
  input  [15:0] A,
  input  [15:0] B,
  input  SUB,
  output OVF,
  output [15:0] Output
);

  wire LSB_carry, n1_bit_adder_1_carry, n1_bit_adder_2_carry, n1_bit_adder_3_carry, n1_bit_adder_4_carry,
       n1_bit_adder_5_carry, n1_bit_adder_6_carry, n1_bit_adder_7_carry, n1_bit_adder_8_carry,
       n1_bit_adder_9_carry, n1_bit_adder_10_carry, n1_bit_adder_11_carry, n1_bit_adder_12_carry,
       n1_bit_adder_13_carry, n1_bit_adder_14_carry, xor_1_out, xor_2_out, xor_3_out, xor_4_out, xor_5_out,
       xor_6_out, xor_7_out, xor_8_out, xor_9_out, xor_10_out, xor_11_out, xor_12_out, xor_13_out,
       xor_14_out, xor_15_out, xor_16_out;

  _1_bit_Adder MSB (.A(A[15]), .B(xor_1_out), .C(n1_bit_adder_1_carry), .SUM(Output[15]), .CARRY(OVF));
  xor xor_1 (xor_1_out, SUB, B[15]);
  xor xor_2 (xor_2_out, SUB, B[14]);
  _1_bit_Adder u_1_bit_adder_1 (
    .A(A[14]), .B(xor_2_out), .C(n1_bit_adder_2_carry), .SUM(Output[14]), .CARRY(n1_bit_adder_1_carry));
  xor xor_3 (xor_3_out, SUB, B[13]);
  _1_bit_Adder u_1_bit_adder_2 (
    .A(A[13]), .B(xor_3_out), .C(n1_bit_adder_3_carry), .SUM(Output[13]), .CARRY(n1_bit_adder_2_carry));
  xor xor_4 (xor_4_out, SUB, B[12]);
  _1_bit_Adder u_1_bit_adder_3 (
    .A(A[12]), .B(xor_4_out), .C(n1_bit_adder_4_carry), .SUM(Output[12]), .CARRY(n1_bit_adder_3_carry));
  xor xor_5 (xor_5_out, SUB, B[11]);
  _1_bit_Adder u_1_bit_adder_4 (
    .A(A[11]), .B(xor_5_out), .C(n1_bit_adder_5_carry), .SUM(Output[11]), .CARRY(n1_bit_adder_4_carry));
  _1_bit_Adder u_1_bit_adder_5 (
    .A(A[10]), .B(xor_6_out), .C(n1_bit_adder_6_carry), .SUM(Output[10]), .CARRY(n1_bit_adder_5_carry));
  xor xor_6 (xor_6_out, SUB, B[10]);
  _1_bit_Adder u_1_bit_adder_6 (
    .A(A[9]), .B(xor_7_out), .C(n1_bit_adder_7_carry), .SUM(Output[9]), .CARRY(n1_bit_adder_6_carry));
  xor xor_7 (xor_7_out, SUB, B[9]);
  _1_bit_Adder u_1_bit_adder_7 (
    .A(A[8]), .B(xor_8_out), .C(n1_bit_adder_8_carry), .SUM(Output[8]), .CARRY(n1_bit_adder_7_carry));
  xor xor_8 (xor_8_out, SUB, B[8]);
  _1_bit_Adder u_1_bit_adder_8 (
    .A(A[7]), .B(xor_9_out), .C(n1_bit_adder_9_carry), .SUM(Output[7]), .CARRY(n1_bit_adder_8_carry));
  xor xor_9 (xor_9_out, SUB, B[7]);
  xor xor_10 (xor_10_out, SUB, B[6]);
  _1_bit_Adder u_1_bit_adder_9 (
    .A(A[6]), .B(xor_10_out), .C(n1_bit_adder_10_carry), .SUM(Output[6]), .CARRY(n1_bit_adder_9_carry));
  xor xor_11 (xor_11_out, SUB, B[5]);
  _1_bit_Adder u_1_bit_adder_10 (
    .A(A[5]), .B(xor_11_out), .C(n1_bit_adder_11_carry), .SUM(Output[5]), .CARRY(n1_bit_adder_10_carry));
  xor xor_12 (xor_12_out, SUB, B[4]);
  _1_bit_Adder u_1_bit_adder_11 (
    .A(A[4]), .B(xor_12_out), .C(n1_bit_adder_12_carry), .SUM(Output[4]), .CARRY(n1_bit_adder_11_carry));
  xor xor_13 (xor_13_out, SUB, B[3]);
  _1_bit_Adder u_1_bit_adder_12 (
    .A(A[3]), .B(xor_13_out), .C(n1_bit_adder_13_carry), .SUM(Output[3]), .CARRY(n1_bit_adder_12_carry));
  _1_bit_Adder u_1_bit_adder_13 (
    .A(A[2]), .B(xor_14_out), .C(n1_bit_adder_14_carry), .SUM(Output[2]), .CARRY(n1_bit_adder_13_carry));
  xor xor_14 (xor_14_out, SUB, B[2]);
  _1_bit_Adder u_1_bit_adder_14 (
    .A(A[1]), .B(xor_15_out), .C(LSB_carry), .SUM(Output[1]), .CARRY(n1_bit_adder_14_carry));
  xor xor_15 (xor_15_out, SUB, B[1]);
  _1_bit_Adder LSB (.A(A[0]), .B(xor_16_out), .C(SUB), .SUM(Output[0]), .CARRY(LSB_carry));
  xor xor_16 (xor_16_out, SUB, B[0]);

  // Notes on the sheet:
  //   NOTES
  //   OPERATION - A - B
  //   Use Cin as 0 to add the numbers
  //   Use Cin as 1 to subtract the numbers
endmodule

module tester (
  input  Basic_Control,
  input  [2:0] in_2,
  input  [2:0] ALUop,
  input  Rwe,
  input  [2:0] Rs,
  input  [2:0] Rt,
  input  [2:0] Rd,
  input  [2:0] Shamt,
  input  [5:0] Immediate,
  input  ALUinB,
  input  Rdst,
  input  Rdst_2,
  input  Dmwe,
  input  Rwd,
  input  Bne,
  output [15:0] out_16,
  output [5:0] Immediate_2
);

  wire Bne_control, Clk, clock_2_out, not_1_out, zerochecker_1_out_3;
  wire [2:0] multiplexer_2_out;
  wire [15:0] alu_1_output, Instruction, leftshift_1_output, multiplexer_1_out, multiplexer_3_out,
       n16_bit_adder_1_output, n16_bit_adder_2_output, pc, ram_1_data, registerfile_1_readdata1,
       registerfile_1_readdata2, SigX, undriven;

  Clock clock_1 (.out(Clk));
  _16_bit_register u_16_bit_register_1 (
    .DATA_IN(multiplexer_1_out), .CLK(Clk), .WE(1'b1), .RS(Basic_Control), .DATA_SAVED(pc));
  _16_bit_Adder u_16_bit_adder_1 (.A(16'h4), .B(pc), .SUB(1'b0), .Output(n16_bit_adder_1_output));  // open: OVF
  ROM #(.addrWidth(16), .dataWidth(16)) rom_1 (.addr(pc), .data(Instruction), .sel(1'b1));
  LeftShift leftshift_1 (.Input(SigX), .SHAMT(in_2), .Output(leftshift_1_output));
  _16_bit_Adder u_16_bit_adder_2 (
    .A(n16_bit_adder_1_output), .B(leftshift_1_output), .SUB(1'b0), .Output(n16_bit_adder_2_output));  // open: OVF
  _16_bit_register u_16_bit_register_2 (.DATA_IN(undriven), .CLK(Clk), .WE(1'b1), .RS(Basic_Control), .DATA_SAVED(pc));
  Multiplexer #(.width(16)) multiplexer_1 (
    .in0(n16_bit_adder_1_output), .in1(n16_bit_adder_2_output), .out(multiplexer_1_out), .sel(Bne_control));  // open: en
  _16_bit_Adder u_16_bit_adder_3 (.A(16'h1), .B(pc), .SUB(1'b0));  // open: OVF, Output
  ROM #(.addrWidth(16), .dataWidth(16)) rom_2 (.addr(pc), .data(Instruction));  // open: sel
  Clock clock_2 (.out(clock_2_out));
  Multiplexer #(.width(3)) multiplexer_2 (.in0(Rd), .in1(Rt), .out(multiplexer_2_out), .sel(Rdst));  // open: en
  RegisterFile registerfile_1 (
    .DATA(out_16), .WE(Rwe), .RESET(Basic_Control), .R1(Rs), .R2(Rt), .WriteReg(multiplexer_2_out),
    .CLK(clock_2_out), .ReadData1(registerfile_1_readdata1), .ReadData2(registerfile_1_readdata2));
  assign SigX = {{10{1'b0}}, Immediate};  // Bit_Extender bit_extender_1
  Multiplexer #(.width(16)) multiplexer_3 (
    .in0(registerfile_1_readdata2), .in1(SigX), .out(multiplexer_3_out), .sel(ALUinB));  // open: en
  ALU alu_1 (
    .OUTPUT(alu_1_output), .INPUT1(registerfile_1_readdata1), .INPUT2(multiplexer_3_out), .OPNUM(ALUop),
    .SHAMT(Shamt));  // open: OVF
  and and_1 (Bne_control, not_1_out, Bne);
  RAM #(.addrWidth(16), .dataWidth(16), .bus("separate")) ram_1 (
    .addr(alu_1_output), .din(registerfile_1_readdata2), .data(ram_1_data), .str(Dmwe), .clk(Clk), .ld(Rdst_2));  // open: sel, clr
  Multiplexer #(.width(16)) multiplexer_4 (.in0(alu_1_output), .in1(ram_1_data), .out(out_16), .sel(Rwd));  // open: en
  not not_1 (not_1_out, zerochecker_1_out_3);
  ZeroChecker zerochecker_1 (.Input(out_16), .out_3(zerochecker_1_out_3), .CONTROL(1'b0));

  // Other names for the same wires on the sheet: Dmre = Rdst_2; Reset = Basic_Control

  // Notes on the sheet:
  //   Get the Instruction and store it in IM
  //   Get the Instruction and store it in IM
endmodule

module \new  (
);

  wire undriven;

  main main_1 (.reset(undriven));
endmodule
